# Fritzing sketch light table (saved by Fritzing 0.9.4)
circuit board: 8.46667cm x 5.64444cm

parts:
  Part1 = Arduino Nano (Rev3.0) (ICSP)
  J1 = Power Jack [package=power_jack_smd]
  U1 = POT [package=pot_alpha_rv16af-20]
  U2 = SWITCH_SPDT [package=kps-1290]
  R1 = Resistor [tolerance=±5% resistance=470 package=THT]
  TP1 = TP4056 [chip_label=TP4056 package="DIP (Dual Inline) [THT]"]
  U3 = Mini-360 DC-DC Buck converter [package=THT]
  U4 = WS2812 RGB LED strip
  BAT1 = 18650 battery holder2 [package=battery-18650-kit]
  C3 = Electrolytic Capacitor [capacitance=1000µF package="300 mil [THT, electrolytic]"]

nets:
  GND: Part1.GND, Part1.A0, J1.GND, U1.A, U1.S, U3.OUT-, U4.GND, C3.-
  N1: Part1.D2, R1.Pin_1
  VIN: Part1.VIN, J1.PWR, U1.E, U3.OUT+, U4.VCC, C3.+
  N2: U2.O, TP1.pin5
  N3: U2.P, U3.IN-
  N4: R1.Pin_0, U4.DIN
  N5: TP1.pin3, U3.IN+
  N6: TP1.pin4, BAT1.+
  N7: TP1.pin6, BAT1.-

custom parts:
  TP4056: A DIP stand-in part for whatever IC you want. With 6 pins on a 300mil dual inline package (DIP) footprint.
  Mini-360 DC-DC Buck converter: Mini-360 DC-DC Buck converter. Tiny buck step down voltage converter, input voltage 4.75 to 23V output 1 to 17V adjustable. Available from ebay and the like.
  WS2812 RGB LED strip: WS2812 strip
  18650 battery holder2: 18650 Battery Holder
